// Digital circuit hw1_multiplier.dig as structural Verilog
module hw1_multiplier (
  input  A0,
  input  A1,
  input  B0,
  input  B1,
  output P1,
  output P0,
  output P2,
  output P3
);

  wire and_2_out, and_3_out, and_4_out, and_5_out, not_1_out, not_2_out;

  not not_1 (not_1_out, A0);
  not not_2 (not_2_out, B0);
  and and_1 (P0, A0, B0);
  and and_2 (and_2_out, A1, B0);
  and and_3 (and_3_out, A0, B1);
  and and_4 (and_4_out, B1, not_1_out, A1);
  and and_5 (and_5_out, B1, not_2_out, A1);
  and and_6 (P3, B1, A0, B0, A1);
  xor xor_1 (P1, and_2_out, and_3_out);
  or or_1 (P2, and_4_out, and_5_out);
endmodule
