// Digital circuit hwonefulladder.dig as structural Verilog
module hwonefulladder (
  input  A,
  input  B,
  input  Cin,
  input  A_2,
  input  B_2,
  input  Cin_2,
  input  A_3,
  input  B_3,
  output SUM,
  output Cout
);

  wire and_1_out, and_2_out, xor_1_out, xor_2_out;

  xor xor_1 (xor_1_out, A, B);
  xor xor_2 (xor_2_out, A_2, B_2);
  and and_1 (and_1_out, A_3, B_3);
  xor xor_3 (SUM, xor_1_out, Cin);
  and and_2 (and_2_out, xor_2_out, Cin_2);
  or or_1 (Cout, and_2_out, and_1_out);
endmodule
