// Digital circuit hwoneripplecarryadder.dig as structural Verilog
module hwoneripplecarryadder (
  input  A0,
  input  B0,
  input  Cin,
  input  A1,
  input  B1,
  input  A2,
  input  B2,
  input  A3,
  input  B3,
  output out_4,
  output out_11,
  output out_12,
  output out_13,
  output out_14
);

  wire bit0_c_o, bit1_c_o, bit2_c_o;

  Add bit0 (.a(A0), .b(B0), .c_i(Cin), .s(out_11), .c_o(bit0_c_o));
  Add bit1 (.a(A1), .b(B1), .c_i(bit0_c_o), .s(out_12), .c_o(bit1_c_o));
  Add bit2 (.a(A2), .b(B2), .c_i(bit1_c_o), .s(out_13), .c_o(bit2_c_o));
  Add bit3 (.a(A3), .b(B3), .c_i(bit2_c_o), .s(out_14), .c_o(out_4));
endmodule
